# Fritzing sketch neopixel (saved by Fritzing 0.9.1b)
breadboards: 1

parts:
  Bauteil1 = Arduino Uno (Rev3)
  NEOPIXEL1 = Neopixel Strip -- White (30/m)

nets:
  GND: Bauteil1.GND, NEOPIXEL1.GND
  N1: Bauteil1.D2, NEOPIXEL1.Din
  5V: Bauteil1.5V, NEOPIXEL1.+5V

custom parts:
  Neopixel Strip -- White (30/m): These NeoPixel strips have 30 digitally-addressable pixel LEDs per meter and are very affordable and are only 12.5 mm wide, 10 mm if you remove the strip from the casing.
